# Fritzing sketch SedentaryWary (saved by Fritzing 0.9.2b)
breadboards: 1

parts:
  Setting_Switch = DIP SWITCH [package=dipswitch-02]
  SW2 = DIP SWITCH [package=dipswitch-02]
  Power_Switch = Toggle Switch [package=THT]
  Button = Pushbutton [package="[THT]"]
  3-Axis_Accelerometer/Gyroscope = 3-Axis Accelerometer Breakout - MMA8452Q
  Buzzer = Piezo Speaker
  part = LED - 5mm [color="Red (633nm)" package="5 mm [THT]"]
  part_2 = Resistor [tolerance=±5% resistance=47 package=THT]
  Power_Switch_2 = Arduino Pro Mini v13
  part_3 = Battery block 9V

nets:
  GND: Setting_Switch.1, Setting_Switch.2, SW2.1, SW2.2, Button.Pin_1, Button.Pin_2, 3-Axis_Accelerometer/Gyroscope.GND, Buzzer.pin2, part.cathode, Power_Switch_2.GND, part_3.-
  N1: Setting_Switch.3, Power_Switch_2.D9_PWM
  N2: Setting_Switch.4, Power_Switch_2.D8
  N3: SW2.3, Power_Switch_2.D7
  N4: SW2.4, Power_Switch_2.D6_PWM
  N5: Power_Switch.COM, part_3.+
  N6: Power_Switch.L2, Power_Switch_2.RAW
  N7: Button.Pin_3, Power_Switch_2.D1/RX
  3.3V: 3-Axis_Accelerometer/Gyroscope.3.3V, Power_Switch_2.VCC
  N8: 3-Axis_Accelerometer/Gyroscope.SDA, Power_Switch_2.A4
  N9: 3-Axis_Accelerometer/Gyroscope.SCL, Power_Switch_2.A5
  N10: Buzzer.pin1, Power_Switch_2.D12/MISO
  N11: part.anode, part_2.Pin_1
  N12: part_2.Pin_0, Power_Switch_2.D3_PWM
